// Logisim project 872815-alu (1).circ as structural Verilog: 7 circuits, main circuit alu
// A
module alu (
  input  [15:0] A,
  input  [15:0] B,
  input  [1:0] T,
  output C,
  output [15:0] S,
  output N,
  output V,
  output Z
);

  wire and_1_out, and_2_out, not_1_out, not_2_out, not_3_out;
  wire [15:0] adder_1_out, b_prime, bit_extender_1_out, xor_1_out;

  assign bit_extender_1_out = {{15{T[1]}}, T[1]};  // Bit_Extender bit_extender_1
  assign b_prime = bit_extender_1_out ^ B;  // XOR_Gate _55, 16 bits wide
  Adder #(.width(16)) adder_1 (.a(A), .b(b_prime), .out(adder_1_out), .cin(T[1]), .cout(C));
  assign xor_1_out = A ^ B;  // XOR_Gate xor_1, 16 bits wide
  not not_1 (not_1_out, N);
  not not_2 (not_2_out, A[15]);
  not not_3 (not_3_out, b_prime[15]);
  MUX_4_1x16 mux_4_1x16_1 (
    .x0(adder_1_out), .x1(xor_1_out), .x2(B), .x3(adder_1_out), .S1(T[0]), .S0(T[1]), .z({N, S[14:0]}));
  and and_1 (and_1_out, not_2_out, N, not_3_out);
  and and_2 (and_2_out, b_prime[15], not_1_out, A[15]);
  or or_1 (V, and_1_out, and_2_out);
  nor nor_1 (Z, S[14], S[13], S[12], S[11], S[10], S[9], S[8], S[7], S[6], S[5], S[4], S[3], S[2], S[1], S[0], N);

  assign S[15] = N;

  // Other names for the same wires on the sheet: a_t = T[0]; b_t = T[1]
endmodule

module mux_4_1 (
  input  S0,
  input  S1,
  input  X0,
  input  X1,
  input  X2,
  input  X3,
  output Z
);

  wire and_1_out, and_2_out, and_3_out, and_4_out, not_1_out, not_2_out;

  not not_1 (not_1_out, S1);
  not not_2 (not_2_out, S0);
  and and_1 (and_1_out, X0, not_2_out, not_1_out);
  and and_2 (and_2_out, X1, not_2_out, S1);
  and and_3 (and_3_out, X2, S0, not_1_out);
  and and_4 (and_4_out, X3, S0, S1);
  or or_1 (Z, and_1_out, and_2_out, and_3_out, and_4_out);
endmodule

module mux_4_1X4 (
  input  [3:0] x0,
  input  [3:0] x1,
  input  [3:0] x2,
  input  [3:0] x3,
  input  S1,
  input  S0,
  output [3:0] out_7
);

  mux_4_1 mux_4_1_1 (.S0(S0), .S1(S1), .X0(x0[0]), .X1(x1[0]), .X2(x2[0]), .X3(x3[0]), .Z(out_7[0]));
  mux_4_1 mux_4_1_2 (.S0(S0), .S1(S1), .X0(x0[1]), .X1(x1[1]), .X2(x2[1]), .X3(x3[1]), .Z(out_7[1]));
  mux_4_1 mux_4_1_3 (.S0(S0), .S1(S1), .X0(x0[2]), .X1(x1[2]), .X2(x2[2]), .X3(x3[2]), .Z(out_7[2]));
  mux_4_1 mux_4_1_4 (.S0(S0), .S1(S1), .X0(x0[3]), .X1(x1[3]), .X2(x2[3]), .X3(x3[3]), .Z(out_7[3]));
endmodule

// 45
module MUX_4_1x16 (
  input  [15:0] x0,
  input  [15:0] x1,
  input  [15:0] x2,
  input  [15:0] x3,
  input  S1,
  input  S0,
  output [15:0] z
);

  mux_4_1X4 mux_4_1x4_1 (.x0(x0[3:0]), .x1(x1[3:0]), .x2(x2[3:0]), .x3(x3[3:0]), .S1(S1), .S0(S0), .out_7(z[3:0]));
  mux_4_1X4 mux_4_1x4_2 (.x0(x0[7:4]), .x1(x1[7:4]), .x2(x2[7:4]), .x3(x3[7:4]), .S1(S1), .S0(S0), .out_7(z[7:4]));
  mux_4_1X4 mux_4_1x4_3 (.x0(x0[11:8]), .x1(x1[11:8]), .x2(x2[11:8]), .x3(x3[11:8]), .S1(S1), .S0(S0), .out_7(z[11:8]));
  mux_4_1X4 mux_4_1x4_4 (
    .x0(x0[15:12]), .x1(x1[15:12]), .x2(x2[15:12]), .x3(x3[15:12]), .S1(S1), .S0(S0), .out_7(z[15:12]));
endmodule

module addGen (
  input  reset,
  input  clk,
  input  ag_en,
  output out_4,
  output out_5,
  output out_6,
  output \end 
);

  wire and_1_out, and_2_out, and_3_out, and_4_out, not_1_out, not_2_out, not_3_out, not_4_out, or_1_out,
       or_2_out, or_3_out, or_4_out, or_5_out;

  not not_1 (not_1_out, out_4);
  not not_2 (not_2_out, out_5);
  not not_3 (not_3_out, ag_en);
  not not_4 (not_4_out, out_6);
  or or_1 (or_1_out, ag_en, out_4);
  or or_2 (or_2_out, out_4, out_5);
  or or_3 (or_3_out, out_4, out_6);
  or or_4 (or_4_out, not_3_out, not_1_out, not_2_out, not_4_out);
  and and_1 (and_1_out, ag_en, out_6, not_2_out);
  and and_2 (and_2_out, not_3_out, out_5);
  and and_3 (and_3_out, not_4_out, out_5);
  or or_5 (or_5_out, and_1_out, and_2_out, and_3_out);
  and and_4 (and_4_out, or_1_out, or_2_out, or_3_out, or_4_out);
  D_Flip_Flop d_ff_1 (.clk(clk), .D(or_5_out), .Q(out_5), .reset(reset));  // open: Qn, preset, en
  T_Flip_Flop t_ff_1 (.clk(clk), .T(ag_en), .Q(out_6), .reset(reset));  // open: Qn, preset, en
  D_Flip_Flop d_ff_2 (.clk(clk), .D(and_4_out), .Q(out_4), .reset(reset));  // open: Qn, preset, en
  and and_5 (\end , out_4, out_5, out_6);

  // Other names for the same wires on the sheet: q0 = out_6; q1 = out_5; q2 = out_4
endmodule

module ALU (
  input  [1:0] flag,
  input  reset,
  input  [1:0] in_3,
  input  [15:0] in_4
);

  wire acc_en, addGen, alu_1_c, alu_1_n, alu_1_v, alu_1_z, clk, \end , mdr_en;
  wire [2:0] addgen_1_out_4;
  wire [15:0] alu_1_s, register_1_q, rom_1_data;

  Clock clock_1 (.out(clk));
  addGen addgen_1 (
    .reset(reset), .clk(clk), .ag_en(addGen), .out_4(addgen_1_out_4[0]), .out_5(addgen_1_out_4[1]),
    .out_6(addgen_1_out_4[2]), .\end (\end ));
  Register #(.width(16)) register_1 (.D(rom_1_data), .en(mdr_en), .Q(register_1_q), .clk(clk), .clr(reset));
  alu alu_1 (.A(register_1_q), .B(in_4), .T(in_3), .S(alu_1_s), .Z(alu_1_z), .C(alu_1_c), .N(alu_1_n), .V(alu_1_v));
  ROM #(.addrWidth(3), .dataWidth(16)) rom_1 (.addr(addgen_1_out_4), .data(rom_1_data));  // open: sel
  Register #(.width(16)) register_2 (.D(alu_1_s), .en(acc_en), .Q(in_4), .clk(clk), .clr(reset));
endmodule

module main (
);

  wire a, alu_1_z, b, clk, FZ, fz_t, ir, nL_E, not_1_out, pc_t, reset;
  wire [1:0] alu, CO, mux;
  wire [3:0] estado, rom_1_data;
  wire [6:0] adder_1_out, D, F, multiplexer_1_out, PC;
  wire [15:0] A_q, alu_1_s, B_q, ram_1_data;

  Register #(.width(4)) u_estado (.D(rom_1_data), .Q(estado), .clk(clk), .clr(reset));  // open: en
  Register #(.width(7)) u_PC (.D(adder_1_out), .en(pc_t), .Q(PC), .clk(clk), .clr(reset));
  Register #(.width(16)) u_IR (.D(ram_1_data), .en(ir), .Q({CO, F, D}), .clk(clk));  // open: clr
  Multiplexer #(.select(2), .width(7), .enable("false")) multiplexer_1 (
    .in0(PC), .in2(F), .in3(D), .out(multiplexer_1_out), .sel(mux));  // open: in1
  ROM #(.addrWidth(7), .dataWidth(4)) rom_1 (.addr({estado, CO, FZ}), .data(rom_1_data));  // open: sel
  ROM #(.addrWidth(4), .dataWidth(10)) rom_2 (
    .addr(estado), .data({mux, alu, nL_E, pc_t, ir, a, b, fz_t}));  // open: sel
  Adder #(.width(7)) adder_1 (.a(7'b0000001), .b(multiplexer_1_out), .out(adder_1_out));  // open: cin, cout
  Register #(.width(16)) u_A (.D(ram_1_data), .en(a), .Q(A_q), .clk(clk));  // open: clr
  Register #(.width(1)) u_FZ (.D(alu_1_z), .en(fz_t), .Q(FZ), .clk(clk));  // open: clr
  alu alu_1 (.A(A_q), .B(B_q), .T(alu), .S(alu_1_s), .Z(alu_1_z));  // open: C, N, V
  // Probe on PC
  // Probe on CO
  Register #(.width(16)) u_B (.D(ram_1_data), .en(b), .Q(B_q), .clk(clk));  // open: clr
  Button button_1 (.out(reset));
  Clock clock_1 (.out(clk));
  // Probe on D
  // Probe on F
  RAM #(.addrWidth(7), .dataWidth(16), .bus("separate")) ram_1 (
    .addr(multiplexer_1_out), .din(alu_1_s), .data(ram_1_data), .str(nL_E), .sel(1'b1), .clk(clk),
    .ld(not_1_out));  // open: clr
  not not_1 (not_1_out, nL_E);
  // Probe on estado

  // Notes on the sheet:
  //   Unidad de Control (cableada 12 estados)
  //   Unidad de Proceso (ruta de datos)
  //   contents of rom_1 (hex, n*v repeats v):
  //   8*1 2 2 3 3 4 4 5 5 8*6 8*8 8*a 0 b 0 b 0 b 0 b 8*7 8*0 8*9 16*0 8*1
  //   contents of rom_2 (hex, n*v repeats v):
  //   18 0 202 202 202 0 304 321 304 41 3a1 318
  //   Control de simulación
  //   0 ADD
  //   1 CMP
  //   2 MOV
  //   3 BEQ
endmodule
