// Logisim project practica 3.circ as structural Verilog: 4 circuits, main circuit main
module main (
  input  x3,
  input  x2,
  input  x1,
  input  x0,
  input  y3,
  input  y2,
  input  y1,
  input  y0
);

  wire a, a1, a2, b, b1, b2, b3, bi0, bi1, bi2, c, c1, c2, d, d1, d2, e, e1, e2, f, f1, f2, g, g1, g2, s, s1,
       s2;

  prueba prueba_1 (.x3(x3), .x2(x2), .x1(x1), .x0(x0), .s(s), .a(a), .b(b), .c(c), .d(d), .e(e), .f(f), .g(g));
  _7_Segment_Display u_7_segment_display_1 (.g(g), .f(f), .a(a), .b(b), .e(e), .d(d), .c(c));  // open: dp
  _7_Segment_Display u_7_segment_display_2 (.g(s));  // open: f, a, b, e, d, c, dp
  prueba prueba_2 (.x3(y3), .x2(y2), .x1(y1), .x0(y0), .s(s1), .a(a1), .b(b1), .c(c1), .d(d1), .e(e1), .f(f1), .g(g1));
  _7_Segment_Display u_7_segment_display_3 (.g(s1));  // open: f, a, b, e, d, c, dp
  _7_Segment_Display u_7_segment_display_4 (.g(g1), .f(f1), .a(a1), .b(b1), .e(e1), .d(d1), .c(c1));  // open: dp
  RCA4 rca4_1 (
    .x3(x3), .y3(y3), .x2(y2), .y2(x2), .x1(y1), .y1(x1), .x0(y0), .y0(x0), .S_4(b3), .S_3(bi2), .S_2(bi1),
    .S(bi0));
  prueba prueba_3 (
    .x3(b3), .x2(bi2), .x1(bi1), .x0(bi0), .s(s2), .a(a2), .b(b2), .c(c2), .d(d2), .e(e2), .f(f2), .g(g2));
  _7_Segment_Display u_7_segment_display_5 (.g(s2));  // open: f, a, b, e, d, c, dp
  _7_Segment_Display u_7_segment_display_6 (.g(g2), .f(f2), .a(a2), .b(b2), .e(e2), .d(d2), .c(c2));  // open: dp
endmodule

module visualizador_de_enteros (
  input  x3,
  input  x2,
  input  x1,
  input  x0,
  output s,
  output a,
  output b,
  output c,
  output d,
  output e,
  output f,
  output g
);

  wire and_1_out, and_2_out, and_3_out, and_4_out, and_5_out, and_6_out, and_7_out, and_8_out, and_9_out,
       and_10_out, and_11_out, and_12_out, and_13_out, and_14_out, and_15_out, and_16_out, and_17_out,
       and_18_out, and_19_out, and_20_out, and_21_out, not_1_out, not_2_out, not_3_out, not_4_out, not_5_out,
       not_6_out, not_7_out, not_8_out, not_9_out, not_10_out, not_11_out, not_12_out, not_13_out,
       not_14_out, not_15_out, not_16_out, not_17_out, not_18_out, not_19_out, not_20_out, not_21_out,
       not_22_out, not_23_out, not_24_out, not_25_out, not_26_out, not_27_out, not_28_out, not_29_out,
       not_30_out, or_4_out, or_5_out, or_6_out;

  and and_1 (and_1_out, x1, not_1_out);
  not not_1 (not_1_out, x0);
  not not_2 (not_2_out, x3);
  and and_2 (and_2_out, not_2_out, x2);
  and and_3 (and_3_out, x3, not_3_out);
  not not_3 (not_3_out, x2);
  and and_4 (and_4_out, x3, not_4_out);
  not not_4 (not_4_out, x1);
  not not_5 (not_5_out, x3);
  and and_5 (and_5_out, not_5_out, not_6_out, x1);
  not not_6 (not_6_out, x2);
  not not_7 (not_7_out, x3);
  and and_6 (and_6_out, not_7_out, x1, x0);
  and and_7 (and_7_out, x3, not_8_out);
  not not_8 (not_8_out, x1);
  and and_8 (and_8_out, x3, x2, not_9_out);
  not not_9 (not_9_out, x0);
  not not_10 (not_10_out, x3);
  and and_9 (and_9_out, not_10_out, x2);
  and and_10 (and_10_out, x3, not_11_out);
  not not_11 (not_11_out, x2);
  and and_11 (and_11_out, x3, not_12_out);
  not not_12 (not_12_out, x1);
  not not_13 (not_13_out, x1);
  not not_14 (not_14_out, x0);
  not not_15 (not_15_out, x3);
  not not_16 (not_16_out, x0);
  and and_12 (and_12_out, x1, not_17_out);
  not not_17 (not_17_out, x0);
  not not_18 (not_18_out, x2);
  and and_13 (and_13_out, x3, not_18_out, not_19_out);
  not not_19 (not_19_out, x0);
  not not_20 (not_20_out, x2);
  and and_14 (and_14_out, not_20_out, x1, x0);
  not not_21 (not_21_out, x3);
  and and_15 (and_15_out, not_21_out, x2, not_22_out);
  not not_22 (not_22_out, x1);
  not not_23 (not_23_out, x3);
  and and_16 (and_16_out, not_23_out, x2, not_24_out);
  not not_24 (not_24_out, x0);
  not not_25 (not_25_out, x2);
  and and_17 (and_17_out, x3, not_25_out, not_26_out);
  not not_26 (not_26_out, x0);
  not not_27 (not_27_out, x2);
  and and_18 (and_18_out, not_27_out, x1);
  and and_19 (and_19_out, x2, not_28_out);
  not not_28 (not_28_out, x1);
  and and_20 (and_20_out, x2, not_29_out);
  not not_29 (not_29_out, x0);
  and and_21 (and_21_out, x3, not_30_out);
  not not_30 (not_30_out, x0);
  or or_1 (a, and_1_out, and_2_out, and_3_out, and_4_out);
  or or_2 (b, and_5_out, and_6_out, and_7_out, and_8_out);
  or or_3 (c, x0, and_9_out, and_10_out, and_11_out);
  or or_4 (or_4_out, x3, x2, x1, x0);
  and and_22 (d, or_4_out, or_5_out, or_6_out);
  or or_5 (or_5_out, x3, not_13_out, not_14_out);
  or or_6 (or_6_out, not_15_out, x2, x1, not_16_out);
  or or_7 (e, and_12_out, and_13_out);
  or or_8 (f, and_14_out, and_15_out, and_16_out, and_17_out);
  or or_9 (g, and_18_out, and_19_out, and_20_out, and_21_out);

  assign s = x3;
endmodule

module prueba (
  input  x3,
  input  x2,
  input  x1,
  input  x0,
  output s,
  output a,
  output b,
  output c,
  output d,
  output e,
  output f,
  output g
);

  wire and_1_out, and_2_out, and_3_out, and_4_out, and_5_out, and_6_out, and_7_out, and_8_out, and_9_out,
       and_10_out, and_11_out, and_12_out, and_13_out, and_14_out, and_15_out, and_16_out, and_17_out,
       and_18_out, and_19_out, and_20_out, and_21_out, and_22_out, and_23_out, and_24_out, not_1_out,
       not_2_out, not_3_out, not_4_out, not_5_out, not_6_out, not_7_out, not_8_out, not_9_out, not_10_out,
       not_11_out, not_12_out, not_13_out, not_14_out, not_15_out, not_16_out, not_17_out, not_18_out,
       not_19_out, not_20_out, not_21_out, not_22_out, not_23_out, not_24_out, not_25_out, not_26_out,
       not_27_out, not_28_out, not_29_out, not_30_out, not_31_out, not_32_out, not_33_out, not_34_out,
       not_35_out, not_36_out, or_3_out, or_4_out;

  not not_1 (not_1_out, x2);
  and and_1 (and_1_out, not_1_out, not_2_out);
  not not_2 (not_2_out, x0);
  not not_3 (not_3_out, x3);
  and and_2 (and_2_out, not_3_out, x1);
  and and_3 (and_3_out, x1, not_4_out);
  not not_4 (not_4_out, x0);
  and and_4 (and_4_out, x2, not_5_out, x0);
  not not_5 (not_5_out, x1);
  and and_5 (and_5_out, x3, not_6_out);
  not not_6 (not_6_out, x2);
  not not_7 (not_7_out, x3);
  and and_6 (and_6_out, not_7_out, not_8_out);
  not not_8 (not_8_out, x2);
  not not_9 (not_9_out, x2);
  and and_7 (and_7_out, not_9_out, not_10_out);
  not not_10 (not_10_out, x1);
  not not_11 (not_11_out, x1);
  and and_8 (and_8_out, not_11_out, not_12_out);
  not not_12 (not_12_out, x0);
  not not_13 (not_13_out, x3);
  and and_9 (and_9_out, not_13_out, x1, x0);
  and and_10 (and_10_out, x3, x2);
  not not_14 (not_14_out, x1);
  not not_15 (not_15_out, x3);
  not not_16 (not_16_out, x2);
  not not_17 (not_17_out, x1);
  not not_18 (not_18_out, x2);
  and and_11 (and_11_out, not_18_out, not_19_out);
  not not_19 (not_19_out, x0);
  not not_20 (not_20_out, x2);
  and and_12 (and_12_out, not_20_out, x1);
  and and_13 (and_13_out, x1, not_21_out);
  not not_21 (not_21_out, x0);
  not not_22 (not_22_out, x1);
  and and_14 (and_14_out, x2, not_22_out, x0);
  not not_23 (not_23_out, x2);
  and and_15 (and_15_out, not_23_out, not_24_out);
  not not_24 (not_24_out, x0);
  and and_16 (and_16_out, x1, not_25_out);
  not not_25 (not_25_out, x0);
  not not_26 (not_26_out, x1);
  and and_17 (and_17_out, not_26_out, not_27_out);
  not not_27 (not_27_out, x0);
  not not_28 (not_28_out, x3);
  and and_18 (and_18_out, not_28_out, x2, not_29_out);
  not not_29 (not_29_out, x1);
  not not_30 (not_30_out, x3);
  and and_19 (and_19_out, not_30_out, x2, not_31_out);
  not not_31 (not_31_out, x0);
  and and_20 (and_20_out, x3, not_32_out, x1);
  not not_32 (not_32_out, x2);
  not not_33 (not_33_out, x2);
  and and_21 (and_21_out, not_33_out, x1);
  and and_22 (and_22_out, x2, not_34_out);
  not not_34 (not_34_out, x1);
  and and_23 (and_23_out, x2, not_35_out);
  not not_35 (not_35_out, x0);
  and and_24 (and_24_out, x3, not_36_out);
  not not_36 (not_36_out, x0);
  or or_1 (a, and_1_out, and_2_out, and_3_out, and_4_out, and_5_out);
  or or_2 (b, and_6_out, and_7_out, and_8_out, and_9_out, and_10_out);
  or or_3 (or_3_out, x3, x2, not_14_out, x0);
  and and_25 (c, or_3_out, or_4_out);
  or or_4 (or_4_out, not_15_out, not_16_out, not_17_out, x0);
  or or_5 (d, and_11_out, and_12_out, and_13_out, and_14_out);
  or or_6 (e, and_15_out, and_16_out);
  or or_7 (f, and_17_out, and_18_out, and_19_out, and_20_out);
  or or_8 (g, and_21_out, and_22_out, and_23_out, and_24_out);

  assign s = x3;
endmodule

module RCA4 (
  input  x0,
  input  y0,
  input  x1,
  input  y1,
  input  x2,
  input  y2,
  input  x3,
  input  y3,
  output S,
  output S_2,
  output S_3,
  output S_4
);

  wire and_1_out, and_2_out, and_3_out, and_4_out, and_5_out, and_6_out, or_1_out, or_2_out, or_3_out,
       xor_1_out, xor_3_out, xor_5_out, xor_7_out;

  xor xor_1 (xor_1_out, x3, y3);
  xor xor_2 (S_4, xor_1_out, or_1_out);
  or or_1 (or_1_out, and_2_out, and_1_out);
  and and_1 (and_1_out, xor_3_out, or_2_out);
  and and_2 (and_2_out, x2, y2);
  xor xor_3 (xor_3_out, x2, y2);
  xor xor_4 (S_3, xor_3_out, or_2_out);
  or or_2 (or_2_out, and_3_out, and_4_out);
  and and_3 (and_3_out, x1, y1);
  and and_4 (and_4_out, xor_5_out, or_3_out);
  xor xor_5 (xor_5_out, x1, y1);
  xor xor_6 (S_2, xor_5_out, or_3_out);
  or or_3 (or_3_out, and_5_out, and_6_out);
  and and_5 (and_5_out, x0, y0);
  and and_6 (and_6_out, xor_7_out, 1'b0);
  xor xor_7 (xor_7_out, x0, y0);
  xor xor_8 (S, xor_7_out, 1'b0);
endmodule
