// Logisim project practica 4.circ as structural Verilog: 4 circuits, main circuit main
// A
module main (
  input  S1,
  input  S0,
  input  [15:0] A,
  input  [15:0] B,
  output out_5
);

  wire nand_1_out;
  wire [14:0] mux_4_1x16_1_z;
  wire [15:0] adder_1_out, bit_extender_1_out, xor_1_out, xor_2_out;

  assign bit_extender_1_out = {{15{1'b0}}, S1};  // Bit_Extender bit_extender_1
  assign xor_1_out = bit_extender_1_out ^ B;  // XOR_Gate xor_1, 16 bits wide
  Adder #(.width(16)) adder_1 (.a(xor_1_out), .b(A), .out(adder_1_out), .cin(S1));  // open: cout
  assign xor_2_out = A ^ B;  // XOR_Gate xor_2, 16 bits wide
  MUX_4_1x16 mux_4_1x16_1 (
    .x0(adder_1_out), .x1(xor_2_out), .x2(B), .x3(adder_1_out), .S1(S1), .S0(S0), .z({out_5, mux_4_1x16_1_z}));
  nand nand_1 (nand_1_out, mux_4_1x16_1_z[14], mux_4_1x16_1_z[13], mux_4_1x16_1_z[12], mux_4_1x16_1_z[11], mux_4_1x16_1_z[10], mux_4_1x16_1_z[9], mux_4_1x16_1_z[8], mux_4_1x16_1_z[7], mux_4_1x16_1_z[6], mux_4_1x16_1_z[5], mux_4_1x16_1_z[4], mux_4_1x16_1_z[3], mux_4_1x16_1_z[2], mux_4_1x16_1_z[1], mux_4_1x16_1_z[0]);

  // Other names for the same wires on the sheet: a_t = S1; b_t = S0
endmodule

module mux_4_1 (
  input  S0,
  input  S1,
  input  X0,
  input  X1,
  input  X2,
  input  X3,
  output Z
);

  wire and_1_out, and_2_out, and_3_out, and_4_out, not_1_out, not_2_out;

  not not_1 (not_1_out, S1);
  not not_2 (not_2_out, S0);
  and and_1 (and_1_out, X0, not_2_out, not_1_out);
  and and_2 (and_2_out, X1, not_2_out, S1);
  and and_3 (and_3_out, X2, S0, not_1_out);
  and and_4 (and_4_out, X3, S0, S1);
  or or_1 (Z, and_1_out, and_2_out, and_3_out, and_4_out);
endmodule

module mux_4_1X4 (
  input  [3:0] x0,
  input  [3:0] x1,
  input  [3:0] x2,
  input  [3:0] x3,
  input  S1,
  input  S0,
  output [3:0] out_7
);

  mux_4_1 mux_4_1_1 (.S0(S0), .S1(S1), .X0(x0[0]), .X1(x1[0]), .X2(x2[0]), .X3(x3[0]), .Z(out_7[0]));
  mux_4_1 mux_4_1_2 (.S0(S0), .S1(S1), .X0(x0[1]), .X1(x1[1]), .X2(x2[1]), .X3(x3[1]), .Z(out_7[1]));
  mux_4_1 mux_4_1_3 (.S0(S0), .S1(S1), .X0(x0[2]), .X1(x1[2]), .X2(x2[2]), .X3(x3[2]), .Z(out_7[2]));
  mux_4_1 mux_4_1_4 (.S0(S0), .S1(S1), .X0(x0[3]), .X1(x1[3]), .X2(x2[3]), .X3(x3[3]), .Z(out_7[3]));
endmodule

module MUX_4_1x16 (
  input  [15:0] x0,
  input  [15:0] x1,
  input  [15:0] x2,
  input  [15:0] x3,
  input  S1,
  input  S0,
  output [15:0] z
);

  mux_4_1X4 mux_4_1x4_1 (.x0(x0[3:0]), .x1(x1[3:0]), .x2(x2[3:0]), .x3(x3[3:0]), .S1(S1), .S0(S0), .out_7(z[3:0]));
  mux_4_1X4 mux_4_1x4_2 (.x0(x0[7:4]), .x1(x1[7:4]), .x2(x2[7:4]), .x3(x3[7:4]), .S1(S1), .S0(S0), .out_7(z[7:4]));
  mux_4_1X4 mux_4_1x4_3 (.x0(x0[11:8]), .x1(x1[11:8]), .x2(x2[11:8]), .x3(x3[11:8]), .S1(S1), .S0(S0), .out_7(z[11:8]));
  mux_4_1X4 mux_4_1x4_4 (
    .x0(x0[15:12]), .x1(x1[15:12]), .x2(x2[15:12]), .x3(x3[15:12]), .S1(S1), .S0(S0), .out_7(z[15:12]));
endmodule
