// Logisim project mosfet.circ as structural Verilog: 1 circuit, main circuit main
module main (
  input  w,
  input  in_2,
  input  in_3,
  output z,
  output y
);

  wire transistor_6_out;

  Transistor transistor_1 (.in(1'b1), .out(z), .gate(w));
  Transistor #(.\type ("n")) transistor_2 (.in(1'b0), .out(z), .gate(w));
  Transistor #(.gate("br")) transistor_3 (.in(1'b1), .out(y), .gate(in_3));
  Transistor transistor_4 (.in(1'b1), .out(y), .gate(in_2));
  Transistor #(.\type ("n")) transistor_5 (.in(transistor_6_out), .out(y), .gate(in_2));
  Transistor #(.\type ("n")) transistor_6 (.in(1'b0), .out(transistor_6_out), .gate(in_3));

  // Other names for the same wires on the sheet: x0 = in_2; x1 = in_3
endmodule
