// Logisim project practica2.circ as structural Verilog: 1 circuit, main circuit main
module main (
  input  in_1,
  input  in_2,
  input  in_3,
  input  in_4,
  output z1,
  output z2,
  output z3
);

  wire and_1_out, and_2_out, and_3_out, and_4_out, and_5_out, and_6_out, and_7_out, and_8_out, and_9_out,
       nor_1_out, nor_2_out, nor_3_out, nor_4_out, nor_5_out, nor_6_out, not_1_out, not_3_out, not_5_out,
       not_7_out, not_9_out, not_11_out, not_13_out, not_15_out, not_17_out, not_19_out, not_21_out,
       not_23_out, not_25_out, not_27_out, not_29_out, not_31_out, or_1_out, or_2_out;

  and and_1 (and_1_out, in_2, in_3, in_4);
  and and_2 (and_2_out, in_1, in_3, in_4);
  and and_3 (and_3_out, in_1, in_2, in_4);
  and and_4 (and_4_out, in_1, in_2, in_3);
  and and_5 (and_5_out, in_1, in_2, in_3, in_4);
  not not_1 (not_1_out, in_2);
  not not_2 (not_1_out, in_2);
  not not_3 (not_3_out, in_3);
  not not_4 (not_3_out, in_3);
  not not_5 (not_5_out, in_4);
  not not_6 (not_5_out, in_4);
  not not_7 (not_7_out, in_1);
  not not_8 (not_7_out, in_1);
  not not_9 (not_9_out, in_3);
  not not_10 (not_9_out, in_3);
  not not_11 (not_11_out, in_4);
  not not_12 (not_11_out, in_4);
  not not_13 (not_13_out, in_1);
  not not_14 (not_13_out, in_1);
  not not_15 (not_15_out, in_2);
  not not_16 (not_15_out, in_2);
  not not_17 (not_17_out, in_4);
  not not_18 (not_17_out, in_4);
  not not_19 (not_19_out, in_1);
  not not_20 (not_19_out, in_1);
  not not_21 (not_21_out, in_2);
  not not_22 (not_21_out, in_2);
  not not_23 (not_23_out, in_3);
  not not_24 (not_23_out, in_3);
  not not_25 (not_25_out, in_1);
  not not_26 (not_25_out, in_1);
  not not_27 (not_27_out, in_2);
  not not_28 (not_27_out, in_2);
  not not_29 (not_29_out, in_3);
  not not_30 (not_29_out, in_3);
  not not_31 (not_31_out, in_4);
  not not_32 (not_31_out, in_4);
  and and_6 (and_6_out, in_1, in_2);
  and and_7 (and_7_out, in_3, in_4);
  and and_8 (and_8_out, in_4, in_1);
  and and_9 (and_9_out, in_2, in_3);
  nor nor_1 (nor_1_out, not_1_out, not_3_out, not_5_out);
  nor nor_2 (nor_2_out, not_7_out, not_9_out, not_11_out);
  nor nor_3 (nor_3_out, not_13_out, not_15_out, not_17_out);
  nor nor_4 (nor_4_out, not_19_out, not_21_out, not_23_out);
  nor nor_5 (nor_5_out, not_25_out, not_27_out, not_29_out, not_31_out);
  or or_1 (or_1_out, and_6_out, and_7_out);
  or or_2 (or_2_out, and_8_out, and_9_out);
  or or_3 (z2, and_1_out, and_2_out, and_3_out, and_4_out, and_5_out);
  nor nor_6 (nor_6_out, nor_1_out, nor_2_out, nor_3_out, nor_4_out, nor_5_out);
  not not_33 (z3, nor_6_out);
  and and_10 (z1, or_1_out, or_2_out);

  // Other names for the same wires on the sheet: a = in_1; b = in_2; c = in_3; d = in_4
endmodule
